// Logisim project Multiplexar4X1.circ as structural Verilog: 1 circuit, main circuit Multiplexador4x1
module Multiplexador4x1 (
  input  S1,
  input  S1_2,
  input  input_0,
  input  Input_1,
  input  Input_2,
  input  Input_3,
  output S
);

  wire and_1_out, and_2_out, and_3_out, and_4_out;

  and and_1 (and_1_out, input_0, ~S1_2, ~S1);  // AND_Gate
  and and_2 (and_2_out, Input_1, ~S1, S1_2);  // AND_Gate
  and and_3 (and_3_out, Input_2, ~S1_2, S1);  // AND_Gate
  and and_4 (and_4_out, Input_3, S1_2, S1);
  or or_1 (S, and_1_out, and_2_out, and_3_out, and_4_out);
endmodule
