// Logisim project Multiplexer 4x1.circ as structural Verilog: 1 circuit, main circuit Multiplexador 4x1
module Multiplexador_4x1 (
  input  S1,
  input  S2,
  input  Input_1,
  input  Input_2,
  input  Input_3,
  input  Input_4,
  output S
);

  wire and_1_out, and_2_out, and_3_out, and_4_out;

  and and_1 (and_1_out, Input_1, ~S2, ~S1);  // AND_Gate
  and and_2 (and_2_out, Input_2, ~S1, S2);  // AND_Gate
  and and_3 (and_3_out, Input_3, S2, ~S1);  // AND_Gate
  and and_4 (and_4_out, Input_4, S2, S1);
  or or_1 (S, and_1_out, and_2_out, and_3_out, and_4_out);
endmodule
