// Logisim project Porta XOR.circ as structural Verilog: 1 circuit, main circuit XOR
module XOR (
  input  A,
  input  B,
  output C
);

  wire and_1_out, and_2_out;

  and and_1 (and_1_out, ~A, B);  // AND_Gate
  and and_2 (and_2_out, A, ~B);  // AND_Gate
  or or_1 (C, and_1_out, and_2_out);
endmodule
