// Logisim project Somador 8 bits(int) +4.circ as structural Verilog: 2 circuits, main circuit Somador 8bits(int)+4
module Somador_8bits_int__4 (
  input  [7:0] Input,
  output [7:0] out_2
);

  wire not_1_out, somador_1_bit_1_carryout, somador_1_bit_2_carryout, somador_1_bit_3_carryout,
       somador_1_bit_4_carryout, somador_1_bit_5_carryout, somador_1_bit_6_carryout, somador_1_bit_7_carryout;

  Somador_1_bit somador_1_bit_1 (
    .A(Input[0]), .B(1'b0), .CarryIN(1'b0), .S(out_2[0]), .CarryOUT(somador_1_bit_1_carryout));
  Somador_1_bit somador_1_bit_2 (
    .A(Input[1]), .B(1'b0), .CarryIN(somador_1_bit_1_carryout), .S(out_2[1]),
    .CarryOUT(somador_1_bit_2_carryout));
  Somador_1_bit somador_1_bit_3 (
    .A(Input[2]), .B(not_1_out), .CarryIN(somador_1_bit_2_carryout), .S(out_2[2]),
    .CarryOUT(somador_1_bit_3_carryout));
  not not_1 (not_1_out, 1'b0);
  Somador_1_bit somador_1_bit_4 (
    .A(Input[3]), .B(1'b0), .CarryIN(somador_1_bit_3_carryout), .S(out_2[3]),
    .CarryOUT(somador_1_bit_4_carryout));
  Somador_1_bit somador_1_bit_5 (
    .A(Input[4]), .B(1'b0), .CarryIN(somador_1_bit_4_carryout), .S(out_2[4]),
    .CarryOUT(somador_1_bit_5_carryout));
  Somador_1_bit somador_1_bit_6 (
    .A(Input[5]), .B(1'b0), .CarryIN(somador_1_bit_5_carryout), .S(out_2[5]),
    .CarryOUT(somador_1_bit_6_carryout));
  Somador_1_bit somador_1_bit_7 (
    .A(Input[6]), .B(1'b0), .CarryIN(somador_1_bit_6_carryout), .S(out_2[6]),
    .CarryOUT(somador_1_bit_7_carryout));
  Somador_1_bit somador_1_bit_8 (
    .A(Input[7]), .B(1'b0), .CarryIN(somador_1_bit_7_carryout), .S(out_2[7]));  // open: CarryOUT
endmodule

module Somador_1_bit (
  input  CarryIN,
  input  A,
  input  B,
  output S,
  output CarryOUT
);

  wire and_1_out, and_2_out, and_3_out, xor_1_out;

  xor xor_1 (xor_1_out, A, B);
  and and_1 (and_1_out, A, B);
  and and_2 (and_2_out, B, CarryIN);
  and and_3 (and_3_out, A, CarryIN);
  xor xor_2 (S, xor_1_out, CarryIN);
  or or_1 (CarryOUT, and_1_out, and_2_out, and_3_out);
endmodule
