// Logisim project Memoria_ROM(read_only_memory).circ as structural Verilog: 1 circuit, main circuit ROM(Read-only-Memory)
module ROM_Read_only_Memory (
  input  [2:0] Key_decoder,
  output [7:0] \Saída 
);

  wire and_1_out, and_2_out, and_3_out, and_4_out, and_5_out, and_6_out, and_7_out, and_8_out;

  and and_1 (and_1_out, Key_decoder[0], Key_decoder[1], Key_decoder[2]);
  or or_1 (\Saída [7], and_1_out, and_4_out, and_5_out, and_8_out);
  and and_2 (and_2_out, Key_decoder[0], Key_decoder[1], ~Key_decoder[2]);  // AND_Gate
  or or_2 (\Saída [6], and_2_out, and_3_out, and_6_out, and_7_out);
  and and_3 (and_3_out, Key_decoder[0], ~Key_decoder[1], Key_decoder[2]);  // AND_Gate
  or or_3 (\Saída [5], and_1_out, and_2_out, and_5_out, and_8_out);
  and and_4 (and_4_out, Key_decoder[0], ~Key_decoder[1], ~Key_decoder[2]);  // AND_Gate
  or or_4 (\Saída [4], and_1_out, and_2_out, and_4_out, and_7_out);
  and and_5 (and_5_out, ~Key_decoder[0], Key_decoder[1], Key_decoder[2]);  // AND_Gate
  or or_5 (\Saída [3], and_1_out, and_2_out, and_3_out, and_6_out);
  and and_6 (and_6_out, ~Key_decoder[0], Key_decoder[1], ~Key_decoder[2]);  // AND_Gate
  and and_7 (and_7_out, ~Key_decoder[0], ~Key_decoder[1], Key_decoder[2]);  // AND_Gate
  or or_6 (\Saída [1], and_1_out, and_4_out, and_5_out, and_7_out);
  or or_7 (\Saída [2], and_1_out, and_3_out, and_4_out, and_6_out);
  and and_8 (and_8_out, ~Key_decoder[0], ~Key_decoder[1], ~Key_decoder[2]);  // AND_Gate
  or or_8 (\Saída [0], and_1_out, and_3_out, and_6_out, and_8_out);

  // Notes on the sheet:
  //   1
  //   2
  //   3
  //   4
  //   5
  //   6
  //   7
  //   8
endmodule
