// Logisim project Memoria Ram.circ as structural Verilog
module Memoria_Ram (
  input  Escrever,
  input  Read,
  input  Reset,
  input  [7:0] Entrada,
  input  [2:0] Key,
  output [7:0] \Saída 
);

  wire and_1_out, and_2_out, Clock_out;
  wire [7:0] \demultiplexer_1_saída , \multiplexer_8x1_1_saída , \registrador_8_bits_1_saída ,
       \registrador_8_bits_2_saída , \registrador_8_bits_3_saída , \registrador_8_bits_4_saída ,
       \registrador_8_bits_5_saída , \registrador_8_bits_6_saída , \registrador_8_bits_7_saída ,
       \registrador_8_bits_8_saída ;

  Clock Clock (.out(Clock_out));
  and and_1 (and_1_out, Clock_out, Escrever);
  Demultiplexer demultiplexer_1 (.Chave(Key), .Clock(and_1_out), .\Saída (\demultiplexer_1_saída ));
  Registrador_8_bits registrador_8_bits_1 (
    .Entrada(Entrada), .Clock(\demultiplexer_1_saída [0]), .Reset(Reset),
    .\Saída (\registrador_8_bits_1_saída ));
  Registrador_8_bits registrador_8_bits_2 (
    .Entrada(Entrada), .Clock(\demultiplexer_1_saída [1]), .Reset(Reset),
    .\Saída (\registrador_8_bits_2_saída ));
  Registrador_8_bits registrador_8_bits_3 (
    .Entrada(Entrada), .Clock(\demultiplexer_1_saída [2]), .Reset(Reset),
    .\Saída (\registrador_8_bits_3_saída ));
  Registrador_8_bits registrador_8_bits_4 (
    .Entrada(Entrada), .Clock(\demultiplexer_1_saída [3]), .Reset(Reset),
    .\Saída (\registrador_8_bits_4_saída ));
  Registrador_8_bits registrador_8_bits_5 (
    .Entrada(Entrada), .Clock(\demultiplexer_1_saída [4]), .Reset(Reset),
    .\Saída (\registrador_8_bits_5_saída ));
  Registrador_8_bits registrador_8_bits_6 (
    .Entrada(Entrada), .Clock(\demultiplexer_1_saída [5]), .Reset(Reset),
    .\Saída (\registrador_8_bits_6_saída ));
  Registrador_8_bits registrador_8_bits_7 (
    .Entrada(Entrada), .Clock(\demultiplexer_1_saída [6]), .Reset(Reset),
    .\Saída (\registrador_8_bits_7_saída ));
  Registrador_8_bits registrador_8_bits_8 (
    .Entrada(Entrada), .Clock(\demultiplexer_1_saída [7]), .Reset(Reset),
    .\Saída (\registrador_8_bits_8_saída ));
  and and_2 (and_2_out, Clock_out, Read);
  Multiplexer_8x1 multiplexer_8x1_1 (
    .Input_1(\registrador_8_bits_1_saída ), .Input_2(\registrador_8_bits_2_saída ),
    .Input_3(\registrador_8_bits_3_saída ), .Input_4(\registrador_8_bits_4_saída ),
    .Input_5(\registrador_8_bits_5_saída ), .Input_6(\registrador_8_bits_6_saída ),
    .Input_7(\registrador_8_bits_7_saída ), .Input_8(\registrador_8_bits_8_saída ), .Key(Key),
    .\Saída (\multiplexer_8x1_1_saída ));
  Registrador_8_bits registrador_8_bits_9 (
    .Entrada(\multiplexer_8x1_1_saída ), .Clock(and_2_out), .Reset(Reset), .\Saída (\Saída ));
endmodule

module Registrador_8_bits (
  input  [7:0] Entrada,
  input  Reset,
  input  Clock,
  output [7:0] \Saída 
);

  Flips_Flops flips_flops_1 (.S(1'b0), .CLK(Clock), .D(Entrada[0]), .reset(Reset), .Q(\Saída [0]));  // open: Q_prime
  Flips_Flops flips_flops_2 (.S(1'b0), .CLK(Clock), .D(Entrada[1]), .reset(Reset), .Q(\Saída [1]));  // open: Q_prime
  Flips_Flops flips_flops_3 (.S(1'b0), .CLK(Clock), .D(Entrada[2]), .reset(Reset), .Q(\Saída [2]));  // open: Q_prime
  Flips_Flops flips_flops_4 (.S(1'b0), .CLK(Clock), .D(Entrada[3]), .reset(Reset), .Q(\Saída [3]));  // open: Q_prime
  Flips_Flops flips_flops_5 (.S(1'b0), .CLK(Clock), .D(Entrada[4]), .reset(Reset), .Q(\Saída [4]));  // open: Q_prime
  Flips_Flops flips_flops_6 (.S(1'b0), .CLK(Clock), .D(Entrada[5]), .reset(Reset), .Q(\Saída [5]));  // open: Q_prime
  Flips_Flops flips_flops_7 (.S(1'b0), .CLK(Clock), .D(Entrada[6]), .reset(Reset), .Q(\Saída [6]));  // open: Q_prime
  Flips_Flops flips_flops_8 (.S(1'b0), .CLK(Clock), .D(Entrada[7]), .reset(Reset), .Q(\Saída [7]));  // open: Q_prime
endmodule

module Multiplexer_8x1 (
  input  [7:0] Input_1,
  input  [7:0] Input_2,
  input  [7:0] Input_3,
  input  [7:0] Input_4,
  input  [7:0] Input_5,
  input  [7:0] Input_6,
  input  [7:0] Input_7,
  input  [7:0] Input_8,
  input  [2:0] Key,
  output [7:0] \Saída 
);

  wire [7:0] multiplexer_2x1_8_bit_1_saida, multiplexer_2x1_8_bit_2_saida, multiplexer_2x1_8_bit_3_saida,
       multiplexer_2x1_8_bit_4_saida, multiplexer_2x1_8_bit_5_saida, multiplexer_2x1_8_bit_6_saida;

  Multiplexer_2x1_8_bit multiplexer_2x1_8_bit_1 (
    .Entrada_1(Input_1), .Entrada_2(Input_2), .Key(Key[0]), .Saida(multiplexer_2x1_8_bit_1_saida));
  Multiplexer_2x1_8_bit multiplexer_2x1_8_bit_2 (
    .Entrada_1(Input_3), .Entrada_2(Input_4), .Key(Key[0]), .Saida(multiplexer_2x1_8_bit_2_saida));
  Multiplexer_2x1_8_bit multiplexer_2x1_8_bit_3 (
    .Entrada_1(Input_5), .Entrada_2(Input_6), .Key(Key[0]), .Saida(multiplexer_2x1_8_bit_3_saida));
  Multiplexer_2x1_8_bit multiplexer_2x1_8_bit_4 (
    .Entrada_1(Input_7), .Entrada_2(Input_8), .Key(Key[0]), .Saida(multiplexer_2x1_8_bit_4_saida));
  Multiplexer_2x1_8_bit multiplexer_2x1_8_bit_5 (
    .Entrada_1(multiplexer_2x1_8_bit_1_saida), .Entrada_2(multiplexer_2x1_8_bit_2_saida), .Key(Key[1]),
    .Saida(multiplexer_2x1_8_bit_5_saida));
  Multiplexer_2x1_8_bit multiplexer_2x1_8_bit_6 (
    .Entrada_1(multiplexer_2x1_8_bit_3_saida), .Entrada_2(multiplexer_2x1_8_bit_4_saida), .Key(Key[1]),
    .Saida(multiplexer_2x1_8_bit_6_saida));
  Multiplexer_2x1_8_bit multiplexer_2x1_8_bit_7 (
    .Entrada_1(multiplexer_2x1_8_bit_5_saida), .Entrada_2(multiplexer_2x1_8_bit_6_saida), .Key(Key[2]),
    .Saida(\Saída ));
endmodule

module Flips_Flops (
  input  S,
  input  CLK,
  input  D,
  input  reset,
  output Q,
  output Q_prime
);

  wire nand_1_out, nand_2_out, nand_3_out, nand_4_out, not_1_out, not_2_out;

  not not_1 (not_1_out, S);
  not not_2 (not_2_out, reset);
  nand nand_1 (nand_1_out, not_1_out, nand_4_out, nand_2_out);
  nand nand_2 (nand_2_out, nand_1_out, CLK, not_2_out);
  nand nand_3 (nand_3_out, nand_2_out, CLK, nand_4_out);
  nand nand_4 (nand_4_out, nand_3_out, D, not_2_out);
  nand nand_5 (Q, not_1_out, nand_2_out, Q_prime);
  nand nand_6 (Q_prime, Q, nand_3_out, not_2_out);
endmodule

module Multiplexer_2x1_8_bit (
  input  [7:0] Entrada_1,
  input  [7:0] Entrada_2,
  input  Key,
  output [7:0] Saida
);

  Multiplexer_2x1_1 multiplexer_2x1_1_1 (.A(Entrada_1[0]), .B(Entrada_2[0]), .S(Key), .Y(Saida[0]));
  Multiplexer_2x1_1 multiplexer_2x1_1_2 (.A(Entrada_1[1]), .B(Entrada_2[1]), .S(Key), .Y(Saida[1]));
  Multiplexer_2x1_1 multiplexer_2x1_1_3 (.A(Entrada_1[2]), .B(Entrada_2[2]), .S(Key), .Y(Saida[2]));
  Multiplexer_2x1_1 multiplexer_2x1_1_4 (.A(Entrada_1[3]), .B(Entrada_2[3]), .S(Key), .Y(Saida[3]));
  Multiplexer_2x1_1 multiplexer_2x1_1_5 (.A(Entrada_1[4]), .B(Entrada_2[4]), .S(Key), .Y(Saida[4]));
  Multiplexer_2x1_1 multiplexer_2x1_1_6 (.A(Entrada_1[5]), .B(Entrada_2[5]), .S(Key), .Y(Saida[5]));
  Multiplexer_2x1_1 multiplexer_2x1_1_7 (.A(Entrada_1[6]), .B(Entrada_2[6]), .S(Key), .Y(Saida[6]));
  Multiplexer_2x1_1 multiplexer_2x1_1_8 (.A(Entrada_1[7]), .B(Entrada_2[7]), .S(Key), .Y(Saida[7]));
endmodule

module Multiplexer_2x1_1 (
  input  A,
  input  B,
  input  S,
  output Y
);

  wire and_1_out, and_2_out;

  and and_1 (and_1_out, A, ~S);  // AND_Gate
  and and_2 (and_2_out, B, S);
  or or_1 (Y, and_1_out, and_2_out);
endmodule

module Demultiplexer (
  input  [2:0] Chave,
  input  Clock,
  output [7:0] \Saída 
);

  and and_1 (\Saída [0], ~Chave[2], ~Chave[1], ~Chave[0], Clock);  // AND_Gate
  and and_2 (\Saída [1], ~Chave[2], ~Chave[1], Chave[0], Clock);  // AND_Gate
  and and_3 (\Saída [2], ~Chave[2], Chave[1], ~Chave[0], Clock);  // AND_Gate
  and and_4 (\Saída [3], ~Chave[2], Chave[1], Chave[0], Clock);  // AND_Gate
  and and_5 (\Saída [4], Chave[2], ~Chave[1], ~Chave[0], Clock);  // AND_Gate
  and and_6 (\Saída [5], Chave[2], ~Chave[1], Chave[0], Clock);  // AND_Gate
  and and_7 (\Saída [6], Chave[2], Chave[1], ~Chave[0], Clock);  // AND_Gate
  and and_8 (\Saída [7], Chave[2], Chave[1], Chave[0], Clock);
endmodule
