// Logisim project Banco de Regs.circ as structural Verilog: 9 circuits, main circuit main
module main (
  input  [2:0] WRT_ADRESS,
  input  R,
  input  W,
  input  [7:0] INPUT,
  input  [2:0] in_5,
  input  [2:0] in_6,
  output [7:0] OUT,
  output [7:0] out_8
);

  wire and_1_out, and_2_out, and_3_out, and_4_out, and_5_out, and_6_out, and_7_out, and_8_out, and_9_out,
       and_10_out, and_11_out, and_12_out, and_13_out, and_14_out, and_15_out, and_16_out, not_1_out,
       not_2_out, not_3_out, not_4_out, not_5_out, not_6_out, not_7_out, not_8_out, not_9_out, not_10_out,
       not_11_out, not_12_out;
  wire [7:0] registrador_1_out_4, registrador_2_out_4, registrador_3_out_4, registrador_4_out_4,
       registrador_5_out_4, registrador_6_out_4, registrador_7_out_4, registrador_8_out_4;

  not not_1 (not_1_out, WRT_ADRESS[0]);
  not not_2 (not_2_out, WRT_ADRESS[1]);
  not not_3 (not_3_out, WRT_ADRESS[2]);
  and and_1 (and_1_out, not_3_out, not_2_out, not_1_out);
  and and_2 (and_2_out, W, and_1_out);
  Registrador registrador_1 (.in_1(INPUT), .out_4(registrador_1_out_4), .in_3(and_2_out), .in_2(R));
  Registrador registrador_2 (.in_1(INPUT), .out_4(registrador_2_out_4), .in_3(and_4_out), .in_2(R));
  not not_4 (not_4_out, WRT_ADRESS[2]);
  not not_5 (not_5_out, WRT_ADRESS[1]);
  and and_3 (and_3_out, not_4_out, not_5_out, WRT_ADRESS[0]);
  and and_4 (and_4_out, W, and_3_out);
  not not_6 (not_6_out, WRT_ADRESS[2]);
  not not_7 (not_7_out, WRT_ADRESS[0]);
  and and_5 (and_5_out, not_6_out, WRT_ADRESS[1], not_7_out);
  and and_6 (and_6_out, W, and_5_out);
  Registrador registrador_3 (.in_1(INPUT), .out_4(registrador_3_out_4), .in_3(and_6_out), .in_2(R));
  Registrador registrador_4 (.in_1(INPUT), .out_4(registrador_4_out_4), .in_3(and_8_out), .in_2(R));
  MULT8X1___8BITS mult8x1_8bits_1 (
    .I0(registrador_1_out_4), .I1(registrador_2_out_4), .I2(registrador_3_out_4), .I3(registrador_4_out_4),
    .I4(registrador_5_out_4), .I5(registrador_6_out_4), .I6(registrador_7_out_4), .I7(registrador_8_out_4),
    .SELETOR(in_5), .out_10(OUT));
  not not_8 (not_8_out, WRT_ADRESS[2]);
  and and_7 (and_7_out, not_8_out, WRT_ADRESS[1], WRT_ADRESS[0]);
  and and_8 (and_8_out, W, and_7_out);
  not not_9 (not_9_out, WRT_ADRESS[1]);
  and and_9 (and_9_out, WRT_ADRESS[2], not_9_out, not_11_out);
  and and_10 (and_10_out, W, and_9_out);
  MULT8X1___8BITS mult8x1_8bits_2 (
    .I0(registrador_1_out_4), .I1(registrador_2_out_4), .I2(registrador_3_out_4), .I3(registrador_4_out_4),
    .I4(registrador_5_out_4), .I5(registrador_6_out_4), .I6(registrador_7_out_4), .I7(registrador_8_out_4),
    .SELETOR(in_6), .out_10(out_8));
  not not_10 (not_10_out, WRT_ADRESS[1]);
  not not_11 (not_11_out, WRT_ADRESS[0]);
  and and_11 (and_11_out, WRT_ADRESS[2], not_10_out, WRT_ADRESS[0]);
  and and_12 (and_12_out, W, and_11_out);
  Registrador registrador_5 (.in_1(INPUT), .out_4(registrador_5_out_4), .in_3(and_10_out), .in_2(R));
  Registrador registrador_6 (.in_1(INPUT), .out_4(registrador_6_out_4), .in_3(and_12_out), .in_2(R));
  and and_13 (and_13_out, W, and_14_out);
  not not_12 (not_12_out, WRT_ADRESS[0]);
  and and_14 (and_14_out, WRT_ADRESS[2], WRT_ADRESS[1], not_12_out);
  and and_15 (and_15_out, W, and_16_out);
  Registrador registrador_7 (.in_1(INPUT), .out_4(registrador_7_out_4), .in_3(and_13_out), .in_2(R));
  Registrador registrador_8 (.in_1(INPUT), .out_4(registrador_8_out_4), .in_3(and_15_out), .in_2(R));
  and and_16 (and_16_out, WRT_ADRESS[2], WRT_ADRESS[1], WRT_ADRESS[0]);
endmodule

module Memoria1bit (
  input  S,
  input  e,
  output Q
);

  wire nand_1_out, nand_2_out, nand_4_out;

  nand nand_1 (nand_1_out, S, e);
  nand nand_2 (nand_2_out, nand_1_out, e);
  nand nand_3 (Q, nand_1_out, nand_4_out);
  nand nand_4 (nand_4_out, Q, nand_2_out);
endmodule

module Memoria8bits (
  input  [7:0] in_1,
  input  in_2,
  output [7:0] out_3
);

  Memoria1bit memoria1bit_1 (.S(in_1[0]), .e(in_2), .Q(out_3[0]));
  Memoria1bit memoria1bit_2 (.S(in_1[1]), .e(in_2), .Q(out_3[1]));
  Memoria1bit memoria1bit_3 (.S(in_1[2]), .e(in_2), .Q(out_3[2]));
  Memoria1bit memoria1bit_4 (.S(in_1[3]), .e(in_2), .Q(out_3[3]));
  Memoria1bit memoria1bit_5 (.S(in_1[4]), .e(in_2), .Q(out_3[4]));
  Memoria1bit memoria1bit_6 (.S(in_1[5]), .e(in_2), .Q(out_3[5]));
  Memoria1bit memoria1bit_7 (.S(in_1[6]), .e(in_2), .Q(out_3[6]));
  Memoria1bit memoria1bit_8 (.S(in_1[7]), .e(in_2), .Q(out_3[7]));
endmodule

module MemoriaEnable (
  input  [7:0] in_1,
  input  in_2,
  output [7:0] out_3
);

  and and_1 (out_3[0], in_1[0], in_2);
  and and_2 (out_3[1], in_1[1], in_2);
  and and_3 (out_3[2], in_1[2], in_2);
  and and_4 (out_3[3], in_1[3], in_2);
  and and_5 (out_3[4], in_1[4], in_2);
  and and_6 (out_3[5], in_1[5], in_2);
  and and_7 (out_3[6], in_1[6], in_2);
  and and_8 (out_3[7], in_1[7], in_2);
endmodule

module Registrador (
  input  [7:0] in_1,
  input  in_2,
  input  in_3,
  output [7:0] out_4
);

  wire [7:0] memoria8bits_1_out_3;

  Memoria8bits memoria8bits_1 (.in_1(in_1), .in_2(in_3), .out_3(memoria8bits_1_out_3));
  MemoriaEnable memoriaenable_1 (.in_1(memoria8bits_1_out_3), .in_2(in_2), .out_3(out_4));
endmodule

module MUX2_1_1BIT (
  input  A,
  input  B,
  input  SELETOR,
  output S
);

  wire and_1_out, and_2_out, not_1_out;

  not not_1 (not_1_out, SELETOR);
  and and_1 (and_1_out, not_1_out, A);
  and and_2 (and_2_out, B, SELETOR);
  or or_1 (S, and_1_out, and_2_out);
endmodule

module MUX2X1_8BITS (
  input  [7:0] I0,
  input  [7:0] I1,
  input  SELETOR,
  output [7:0] S
);

  MUX2_1_1BIT mux2_1_1bit_1 (.A(I1[0]), .B(I0[0]), .SELETOR(SELETOR), .S(S[0]));
  MUX2_1_1BIT mux2_1_1bit_2 (.A(I1[1]), .B(I0[1]), .SELETOR(SELETOR), .S(S[1]));
  MUX2_1_1BIT mux2_1_1bit_3 (.A(I1[2]), .B(I0[2]), .SELETOR(SELETOR), .S(S[2]));
  MUX2_1_1BIT mux2_1_1bit_4 (.A(I1[3]), .B(I0[3]), .SELETOR(SELETOR), .S(S[3]));
  MUX2_1_1BIT mux2_1_1bit_5 (.A(I1[4]), .B(I0[4]), .SELETOR(SELETOR), .S(S[4]));
  MUX2_1_1BIT mux2_1_1bit_6 (.A(I1[5]), .B(I0[5]), .SELETOR(SELETOR), .S(S[5]));
  MUX2_1_1BIT mux2_1_1bit_7 (.A(I1[6]), .B(I0[6]), .SELETOR(SELETOR), .S(S[6]));
  MUX2_1_1BIT mux2_1_1bit_8 (.A(I1[7]), .B(I0[7]), .SELETOR(SELETOR), .S(S[7]));
endmodule

module MUX4X1_8BITS (
  input  [7:0] I0,
  input  [7:0] I1,
  input  [7:0] I2,
  input  [7:0] I3,
  input  [1:0] SELETOR,
  output [7:0] out_6
);

  wire [7:0] mux2x1_8bits_1_s, mux2x1_8bits_2_s;

  MUX2X1_8BITS mux2x1_8bits_1 (.S(mux2x1_8bits_1_s), .I0(I1), .I1(I0), .SELETOR(SELETOR[0]));
  MUX2X1_8BITS mux2x1_8bits_2 (.S(mux2x1_8bits_2_s), .I0(I3), .I1(I2), .SELETOR(SELETOR[0]));
  MUX2X1_8BITS mux2x1_8bits_3 (.S(out_6), .I0(mux2x1_8bits_2_s), .I1(mux2x1_8bits_1_s), .SELETOR(SELETOR[1]));
endmodule

module MULT8X1___8BITS (
  input  [7:0] I0,
  input  [7:0] I1,
  input  [7:0] I2,
  input  [7:0] I3,
  input  [7:0] I4,
  input  [7:0] I5,
  input  [7:0] I6,
  input  [7:0] I7,
  input  [2:0] SELETOR,
  output [7:0] out_10
);

  wire [7:0] mux4x1_8bits_1_out_6, mux4x1_8bits_2_out_6;

  MUX4X1_8BITS mux4x1_8bits_1 (
    .I0(I0), .I1(I1), .I2(I2), .I3(I3), .SELETOR(SELETOR[1:0]), .out_6(mux4x1_8bits_1_out_6));
  MUX4X1_8BITS mux4x1_8bits_2 (
    .I0(I4), .I1(I5), .I2(I6), .I3(I7), .SELETOR(SELETOR[1:0]), .out_6(mux4x1_8bits_2_out_6));
  MUX2X1_8BITS mux2x1_8bits_1 (.S(out_10), .I0(mux4x1_8bits_2_out_6), .I1(mux4x1_8bits_1_out_6), .SELETOR(SELETOR[2]));
endmodule
