// Logisim project Flip Flop T(Toggle).circ as structural Verilog: 1 circuit, main circuit flipflop T
module flipflop_T (
  input  Preset,
  input  J,
  input  Clock,
  input  Clear,
  output Q,
  output nQ
);

  wire nand_1_out, nand_2_out, nand_3_out, nand_4_out, nand_6_out, nand_7_out, not_1_out, not_2_out,
       not_3_out;

  not not_1 (not_1_out, Preset);
  nand nand_1 (nand_1_out, nQ, J, Clock);
  not not_2 (not_2_out, Clock);
  not not_3 (not_3_out, Clear);
  nand nand_2 (nand_2_out, Clock, J, Q);
  nand nand_3 (nand_3_out, not_1_out, nand_1_out, nand_4_out);
  nand nand_4 (nand_4_out, nand_3_out, nand_2_out, not_3_out);
  nand nand_5 (Q, nand_6_out, nQ);
  nand nand_6 (nand_6_out, nand_3_out, not_2_out);
  nand nand_7 (nand_7_out, not_2_out, nand_4_out);
  nand nand_8 (nQ, Q, nand_7_out);
endmodule
