// Logisim project Flip Flop JK(Mestre-Escravo).circ as structural Verilog: 1 circuit, main circuit Flip Flop JK(Mestre-Escravo)
module Flip_Flop_JK_Mestre_Escravo (
  input  in_1,
  input  in_2,
  input  in_3,
  input  in_4,
  output out_5,
  output out_6
);

  wire button_1_out, nand_1_out, nand_2_out, nand_3_out, nand_4_out, nand_5_out, nand_6_out, not_1_out;

  Button button_1 (.out(button_1_out));
  not not_1 (not_1_out, button_1_out);
  nand nand_1 (nand_1_out, in_2, button_1_out, out_6);
  nand nand_2 (nand_2_out, out_5, button_1_out, in_3);
  nand nand_3 (nand_3_out, in_1, nand_1_out, nand_4_out);
  nand nand_4 (nand_4_out, nand_3_out, nand_2_out, in_4);
  nand nand_5 (nand_5_out, not_1_out, nand_3_out);
  nand nand_6 (nand_6_out, nand_4_out, not_1_out);
  nand nand_7 (out_5, in_1, nand_5_out, out_6);
  nand nand_8 (out_6, out_5, nand_6_out, in_4);
endmodule
