// Logisim project 11-Extensor.circ as structural Verilog: 2 circuits, main circuit main
module main (
  input  [3:0] in_1,
  input  [3:0] in_2,
  output [7:0] out_3
);


  assign out_3 = {in_2, in_1};
endmodule

module Extensor_de_sinal_4_8bits (
  input  [3:0] Entrada_4_bits,
  output [7:0] out_2
);


  assign out_2 = {{5{Entrada_4_bits[3]}}, Entrada_4_bits[2:0]};
endmodule
