// Logisim project 13_Contador-Sincrono.circ as structural Verilog: 2 circuits, main circuit Contador Sincrono
module Contador_Sincrono (
  input  RESET,
  output Q0,
  output Q1,
  output Q2,
  output Q3
);

  wire and_1_out, and_2_out, clock_1_out;

  Clock clock_1 (.out(clock_1_out));
  Flip_Flop_T flip_flop_t_1 (.Preset(1'b0), .J(1'b1), .Clock(clock_1_out), .Clear(RESET), .Q(Q0));  // open: nQ
  Flip_Flop_T flip_flop_t_2 (.Preset(1'b0), .J(Q0), .Clock(clock_1_out), .Clear(RESET), .Q(Q1));  // open: nQ
  and and_1 (and_1_out, Q0, Q1);
  Flip_Flop_T flip_flop_t_3 (.Preset(1'b0), .J(and_1_out), .Clock(clock_1_out), .Clear(RESET), .Q(Q2));  // open: nQ
  and and_2 (and_2_out, and_1_out, Q2);
  Flip_Flop_T flip_flop_t_4 (.Preset(1'b0), .J(and_2_out), .Clock(clock_1_out), .Clear(RESET), .Q(Q3));  // open: nQ

  // Notes on the sheet:
  //   CLOCK
endmodule

module Flip_Flop_T (
  input  Preset,
  input  J,
  input  Clock,
  input  Clear,
  output Q,
  output nQ
);

  wire nand_1_out, nand_2_out, nand_3_out, nand_4_out, nand_5_out, nand_8_out, not_1_out, not_2_out,
       not_3_out;

  not not_1 (not_1_out, Preset);
  nand nand_1 (nand_1_out, nQ, J, Clock);
  not not_2 (not_2_out, Clock);
  nand nand_2 (nand_2_out, Clock, J, Q);
  not not_3 (not_3_out, Clear);
  nand nand_3 (nand_3_out, not_1_out, nand_1_out, nand_4_out);
  nand nand_4 (nand_4_out, nand_3_out, nand_2_out, not_3_out);
  nand nand_5 (nand_5_out, nand_3_out, not_2_out);
  nand nand_6 (Q, nand_5_out, nQ);
  nand nand_7 (nQ, Q, nand_8_out);
  nand nand_8 (nand_8_out, not_2_out, nand_4_out);
endmodule
