// Logisim project 14_Detector-Impar.circ as structural Verilog: 2 circuits, main circuit Detector Paridade Ímpar
module \Detector_Paridade_Ímpar  (
  input  [7:0] ENTRADA,
  output S
);

  wire porta_xor_1_c, porta_xor_2_c, porta_xor_3_c, porta_xor_4_c, porta_xor_6_c, porta_xor_7_c;

  Porta_XOR porta_xor_1 (.A(ENTRADA[6]), .B(ENTRADA[7]), .C(porta_xor_1_c));
  Porta_XOR porta_xor_2 (.A(ENTRADA[2]), .B(ENTRADA[3]), .C(porta_xor_2_c));
  Porta_XOR porta_xor_3 (.A(ENTRADA[4]), .B(ENTRADA[5]), .C(porta_xor_3_c));
  Porta_XOR porta_xor_4 (.A(porta_xor_3_c), .B(porta_xor_1_c), .C(porta_xor_4_c));
  Porta_XOR porta_xor_5 (.A(porta_xor_7_c), .B(porta_xor_4_c), .C(S));
  Porta_XOR porta_xor_6 (.A(ENTRADA[0]), .B(ENTRADA[1]), .C(porta_xor_6_c));
  Porta_XOR porta_xor_7 (.A(porta_xor_6_c), .B(porta_xor_2_c), .C(porta_xor_7_c));
endmodule

module Porta_XOR (
  input  A,
  input  B,
  output C
);

  wire and_1_out, and_2_out;

  and and_1 (and_1_out, ~A, B);  // AND_Gate
  and and_2 (and_2_out, A, ~B);  // AND_Gate
  or or_1 (C, and_1_out, and_2_out);
endmodule
