// Logisim project Somador_Completo.circ as structural Verilog
module Somador_de_8_bits (
  input  [7:0] Entrada_1,
  input  [7:0] Entrada_2,
  output out_3,
  output [7:0] \Saída 
);

  wire somador_completo_2_cout, somador_completo_3_cout, somador_completo_4_cout, somador_completo_5_cout,
       somador_completo_6_cout, somador_completo_7_cout, somador_completo_8_cout;

  somador_completo somador_completo_1 (
    .A(Entrada_1[7]), .B(Entrada_2[7]), .Cin(somador_completo_2_cout), .S(\Saída [7]), .Cout(out_3));
  somador_completo somador_completo_2 (
    .A(Entrada_1[6]), .B(Entrada_2[6]), .Cin(somador_completo_3_cout), .S(\Saída [6]),
    .Cout(somador_completo_2_cout));
  somador_completo somador_completo_3 (
    .A(Entrada_1[5]), .B(Entrada_2[5]), .Cin(somador_completo_4_cout), .S(\Saída [5]),
    .Cout(somador_completo_3_cout));
  somador_completo somador_completo_4 (
    .A(Entrada_1[4]), .B(Entrada_2[4]), .Cin(somador_completo_5_cout), .S(\Saída [4]),
    .Cout(somador_completo_4_cout));
  somador_completo somador_completo_5 (
    .A(Entrada_1[3]), .B(Entrada_2[3]), .Cin(somador_completo_6_cout), .S(\Saída [3]),
    .Cout(somador_completo_5_cout));
  somador_completo somador_completo_6 (
    .A(Entrada_1[2]), .B(Entrada_2[2]), .Cin(somador_completo_7_cout), .S(\Saída [2]),
    .Cout(somador_completo_6_cout));
  somador_completo somador_completo_7 (
    .A(Entrada_1[1]), .B(Entrada_2[1]), .Cin(somador_completo_8_cout), .S(\Saída [1]),
    .Cout(somador_completo_7_cout));
  somador_completo somador_completo_8 (
    .A(Entrada_1[0]), .B(Entrada_2[0]), .Cin(1'b0), .S(\Saída [0]), .Cout(somador_completo_8_cout));
endmodule

module somador_completo (
  input  A,
  input  B,
  input  Cin,
  output S,
  output Cout
);

  wire and_1_out, and_2_out, xor_1_out_3;

  XOR xor_1 (.A(A), .B(B), .out_3(xor_1_out_3));
  XOR xor_2 (.A(xor_1_out_3), .B(Cin), .out_3(S));
  and and_1 (and_1_out, Cin, xor_1_out_3);
  and and_2 (and_2_out, B, A);
  or or_1 (Cout, and_1_out, and_2_out);
endmodule

module XOR (
  input  A,
  input  B,
  output out_3
);

  wire and_1_out, nor_1_out;

  and and_1 (and_1_out, A, B);
  nor nor_1 (nor_1_out, B, A);
  nor nor_2 (out_3, and_1_out, nor_1_out);
endmodule
