// Logisim project ULA_8_bits.circ as structural Verilog: 10 circuits, main circuit main
// Somador
module Somador_de_8_bits (
  input  [7:0] Entrada_1,
  input  [7:0] Entrada_2,
  output [7:0] \Saída 
);

  wire somador_completo_2_cout, somador_completo_3_cout, somador_completo_4_cout, somador_completo_5_cout,
       somador_completo_6_cout, somador_completo_7_cout, somador_completo_8_cout;

  somador_completo somador_completo_1 (
    .A(Entrada_1[7]), .B(Entrada_2[7]), .Cin(somador_completo_2_cout), .S(\Saída [7]));  // open: Cout
  somador_completo somador_completo_2 (
    .A(Entrada_1[6]), .B(Entrada_2[6]), .Cin(somador_completo_3_cout), .S(\Saída [6]),
    .Cout(somador_completo_2_cout));
  somador_completo somador_completo_3 (
    .A(Entrada_1[5]), .B(Entrada_2[5]), .Cin(somador_completo_4_cout), .S(\Saída [5]),
    .Cout(somador_completo_3_cout));
  somador_completo somador_completo_4 (
    .A(Entrada_1[4]), .B(Entrada_2[4]), .Cin(somador_completo_5_cout), .S(\Saída [4]),
    .Cout(somador_completo_4_cout));
  somador_completo somador_completo_5 (
    .A(Entrada_1[3]), .B(Entrada_2[3]), .Cin(somador_completo_6_cout), .S(\Saída [3]),
    .Cout(somador_completo_5_cout));
  somador_completo somador_completo_6 (
    .A(Entrada_1[2]), .B(Entrada_2[2]), .Cin(somador_completo_7_cout), .S(\Saída [2]),
    .Cout(somador_completo_6_cout));
  somador_completo somador_completo_7 (
    .A(Entrada_1[1]), .B(Entrada_2[1]), .Cin(somador_completo_8_cout), .S(\Saída [1]),
    .Cout(somador_completo_7_cout));
  somador_completo somador_completo_8 (
    .A(Entrada_1[0]), .B(Entrada_2[0]), .Cin(1'b0), .S(\Saída [0]), .Cout(somador_completo_8_cout));
endmodule

module somador_completo (
  input  A,
  input  B,
  input  Cin,
  output S,
  output Cout
);

  wire and_1_out, and_2_out, xor_1_out_3;

  XOR xor_1 (.A(A), .B(B), .out_3(xor_1_out_3));
  XOR xor_2 (.A(xor_1_out_3), .B(Cin), .out_3(S));
  and and_1 (and_1_out, Cin, xor_1_out_3);
  and and_2 (and_2_out, B, A);
  or or_1 (Cout, and_1_out, and_2_out);
endmodule

module XOR (
  input  A,
  input  B,
  output out_3
);

  wire and_1_out, nor_1_out;

  and and_1 (and_1_out, A, B);
  nor nor_1 (nor_1_out, B, A);
  nor nor_2 (out_3, and_1_out, nor_1_out);
endmodule

module main (
  input  [7:0] Entrada_A,
  input  [7:0] Entrada_B,
  input  [3:0] OP_CODE,
  output [7:0] out_4,
  output OverFlow
);

  wire somador_subtrator_1_out_5, somador_subtrator_2_out_5;
  wire [7:0] and_1_out, deslocador_2bit_1_out_3, deslocador_2bit_2_out_3, deslocador_2bit_3_out_3,
       deslocador_2bit_4_out_3, \multiplexer_8x1_8bit_1_saída , \multiplexer_8x1_8bit_2_saída , nand_1_out,
       nor_1_out, not_1_out, not_2_out, or_1_out, somador_subtrator_1_out_4, somador_subtrator_2_out_4,
       xor_1_out;

  Deslocador_2bit deslocador_2bit_1 (.in_1(Entrada_A), .Shift_Left_or_Right(1'b0), .out_3(deslocador_2bit_1_out_3));
  Deslocador_2bit deslocador_2bit_2 (.in_1(Entrada_A), .Shift_Left_or_Right(1'b0), .out_3(deslocador_2bit_2_out_3));
  Deslocador_2bit deslocador_2bit_3 (.in_1(Entrada_A), .Shift_Left_or_Right(1'b1), .out_3(deslocador_2bit_3_out_3));
  Deslocador_2bit deslocador_2bit_4 (.in_1(Entrada_A), .Shift_Left_or_Right(1'b1), .out_3(deslocador_2bit_4_out_3));
  Somador_Subtrator somador_subtrator_1 (
    .Entrada_2(Entrada_B), .out_4(somador_subtrator_1_out_4), .out_5(somador_subtrator_1_out_5),
    .in_2(Entrada_A), .M(1'b0));
  Somador_Subtrator somador_subtrator_2 (
    .Entrada_2(Entrada_B), .out_4(somador_subtrator_2_out_4), .out_5(somador_subtrator_2_out_5),
    .in_2(Entrada_A), .M(1'b1));
  assign and_1_out = Entrada_A & Entrada_B;  // AND_Gate and_1, 8 bits wide
  assign or_1_out = Entrada_A | Entrada_B;  // OR_Gate or_1, 8 bits wide
  assign not_1_out = ~Entrada_A;  // NOT_Gate not_1, 8 bits wide
  assign not_2_out = ~Entrada_B;  // NOT_Gate not_2, 8 bits wide
  assign nor_1_out = ~(Entrada_A | Entrada_B);  // NOR_Gate nor_1, 8 bits wide
  assign nand_1_out = ~(Entrada_A & Entrada_B);  // NAND_Gate nand_1, 8 bits wide
  assign xor_1_out = Entrada_A ^ Entrada_B;  // XOR_Gate xor_1, 8 bits wide
  Multiplexer_8x1_8bit multiplexer_8x1_8bit_1 (
    .Input_1(and_1_out), .Input_2(or_1_out), .Input_3(not_1_out), .Input_4(not_2_out), .Input_5(nor_1_out),
    .Input_6(nand_1_out), .Input_7(xor_1_out), .Input_8(deslocador_2bit_1_out_3), .Key(OP_CODE[2:0]),
    .\Saída (\multiplexer_8x1_8bit_1_saída ));
  Multiplexer_8x1_8bit multiplexer_8x1_8bit_2 (
    .Input_1(deslocador_2bit_2_out_3), .Input_2(deslocador_2bit_3_out_3), .Input_3(deslocador_2bit_4_out_3),
    .Input_4(somador_subtrator_1_out_4), .Input_5(somador_subtrator_2_out_4), .Key(OP_CODE[2:0]),
    .\Saída (\multiplexer_8x1_8bit_2_saída ));  // open: Input_6, Input_7, Input_8
  Multiplexer_2x1_bit multiplexer_2x1_bit_1 (
    .A(somador_subtrator_1_out_5), .B(somador_subtrator_2_out_5), .S(OP_CODE[2]), .Y(OverFlow));
  Multiplexer_2_in_1_out__8bit multiplexer_2_in_1_out_8bit_1 (
    .Entrada_1(\multiplexer_8x1_8bit_1_saída ), .Entrada_2(\multiplexer_8x1_8bit_2_saída ), .Key(OP_CODE[3]),
    .Saida(out_4));

  // Notes on the sheet:
  //   AND - 0000
  //   OR - 0001
  //   NOT A - 0010
  //   NOT B - 0011
  //   NOR - 0100
  //   NAND - 0101
  //   XOR - 0110
  //   SHIFT LEFT A - 0111
  //   Código das Chaves
  //   SHIFT LEFT B - 1000
  //   SHIFT RIGHT A- 1001
  //   SHIFT RIGHT B - 1010
  //   SOMA - 1011
  //   SUBTRAÇÃO 1100
endmodule

module Somador_Subtrator (
  input  M,
  input  [7:0] in_2,
  input  [7:0] Entrada_2,
  output [7:0] out_4,
  output out_5
);

  wire somador_completo_1_cout, somador_completo_2_cout, somador_completo_3_cout, somador_completo_4_cout,
       somador_completo_5_cout, somador_completo_6_cout, somador_completo_7_cout, somador_completo_8_cout,
       xor_1_out_3, xor_2_out_3, xor_3_out_3, xor_4_out_3, xor_5_out_3, xor_6_out_3, xor_7_out_3, xor_8_out_3;

  XOR xor_1 (.A(Entrada_2[0]), .B(M), .out_3(xor_1_out_3));
  XOR xor_2 (.A(Entrada_2[1]), .B(M), .out_3(xor_2_out_3));
  XOR xor_3 (.A(Entrada_2[2]), .B(M), .out_3(xor_3_out_3));
  XOR xor_4 (.A(Entrada_2[3]), .B(M), .out_3(xor_4_out_3));
  XOR xor_5 (.A(Entrada_2[4]), .B(M), .out_3(xor_5_out_3));
  XOR xor_6 (.A(Entrada_2[5]), .B(M), .out_3(xor_6_out_3));
  XOR xor_7 (.A(Entrada_2[6]), .B(M), .out_3(xor_7_out_3));
  XOR xor_8 (.A(Entrada_2[7]), .B(M), .out_3(xor_8_out_3));
  somador_completo somador_completo_1 (
    .A(in_2[0]), .B(xor_1_out_3), .Cin(M), .S(out_4[0]), .Cout(somador_completo_1_cout));
  somador_completo somador_completo_2 (
    .A(in_2[1]), .B(xor_2_out_3), .Cin(somador_completo_1_cout), .S(out_4[1]), .Cout(somador_completo_2_cout));
  somador_completo somador_completo_3 (
    .A(in_2[2]), .B(xor_3_out_3), .Cin(somador_completo_2_cout), .S(out_4[2]), .Cout(somador_completo_3_cout));
  somador_completo somador_completo_4 (
    .A(in_2[3]), .B(xor_4_out_3), .Cin(somador_completo_3_cout), .S(out_4[3]), .Cout(somador_completo_4_cout));
  somador_completo somador_completo_5 (
    .A(in_2[4]), .B(xor_5_out_3), .Cin(somador_completo_4_cout), .S(out_4[4]), .Cout(somador_completo_5_cout));
  somador_completo somador_completo_6 (
    .A(in_2[5]), .B(xor_6_out_3), .Cin(somador_completo_5_cout), .S(out_4[5]), .Cout(somador_completo_6_cout));
  somador_completo somador_completo_7 (
    .A(in_2[6]), .B(xor_7_out_3), .Cin(somador_completo_6_cout), .S(out_4[6]), .Cout(somador_completo_7_cout));
  somador_completo somador_completo_8 (
    .A(in_2[7]), .B(xor_8_out_3), .Cin(somador_completo_7_cout), .S(out_4[7]), .Cout(somador_completo_8_cout));
  XOR xor_9 (.A(somador_completo_8_cout), .B(M), .out_3(out_5));
endmodule

module Deslocador_1bit (
  input  [7:0] in_1,
  input  Clock,
  output [7:0] saida
);

  wire and_1_out, and_2_out, and_4_out, and_5_out, and_6_out, and_7_out, and_8_out, and_9_out, and_10_out,
       and_11_out, and_12_out, and_14_out, not_1_out;

  not not_1 (not_1_out, Clock);
  and and_1 (and_1_out, in_1[0], Clock);
  and and_2 (and_2_out, in_1[1], Clock);
  and and_3 (saida[0], not_1_out, in_1[1]);
  or or_1 (saida[1], and_1_out, and_5_out);
  and and_4 (and_4_out, in_1[2], Clock);
  and and_5 (and_5_out, not_1_out, in_1[2]);
  or or_2 (saida[2], and_2_out, and_7_out);
  and and_6 (and_6_out, in_1[3], Clock);
  and and_7 (and_7_out, not_1_out, in_1[3]);
  or or_3 (saida[3], and_4_out, and_9_out);
  and and_8 (and_8_out, in_1[4], Clock);
  and and_9 (and_9_out, not_1_out, in_1[4]);
  or or_4 (saida[4], and_6_out, and_10_out);
  and and_10 (and_10_out, not_1_out, in_1[5]);
  and and_11 (and_11_out, in_1[5], Clock);
  or or_5 (saida[5], and_8_out, and_12_out);
  and and_12 (and_12_out, not_1_out, in_1[6]);
  and and_13 (saida[7], in_1[6], Clock);
  or or_6 (saida[6], and_11_out, and_14_out);
  and and_14 (and_14_out, not_1_out, in_1[7]);
endmodule

module Multiplexer_2x1_bit (
  input  A,
  input  B,
  input  S,
  output Y
);

  wire and_1_out, and_2_out;

  and and_1 (and_1_out, A, ~S);  // AND_Gate
  and and_2 (and_2_out, B, S);
  or or_1 (Y, and_1_out, and_2_out);
endmodule

module Multiplexer_2_in_1_out__8bit (
  input  [7:0] Entrada_1,
  input  [7:0] Entrada_2,
  input  Key,
  output [7:0] Saida
);

  Multiplexer_2x1_bit multiplexer_2x1_bit_1 (.A(Entrada_1[0]), .B(Entrada_2[0]), .S(Key), .Y(Saida[0]));
  Multiplexer_2x1_bit multiplexer_2x1_bit_2 (.A(Entrada_1[1]), .B(Entrada_2[1]), .S(Key), .Y(Saida[1]));
  Multiplexer_2x1_bit multiplexer_2x1_bit_3 (.A(Entrada_1[2]), .B(Entrada_2[2]), .S(Key), .Y(Saida[2]));
  Multiplexer_2x1_bit multiplexer_2x1_bit_4 (.A(Entrada_1[3]), .B(Entrada_2[3]), .S(Key), .Y(Saida[3]));
  Multiplexer_2x1_bit multiplexer_2x1_bit_5 (.A(Entrada_1[4]), .B(Entrada_2[4]), .S(Key), .Y(Saida[4]));
  Multiplexer_2x1_bit multiplexer_2x1_bit_6 (.A(Entrada_1[5]), .B(Entrada_2[5]), .S(Key), .Y(Saida[5]));
  Multiplexer_2x1_bit multiplexer_2x1_bit_7 (.A(Entrada_1[6]), .B(Entrada_2[6]), .S(Key), .Y(Saida[6]));
  Multiplexer_2x1_bit multiplexer_2x1_bit_8 (.A(Entrada_1[7]), .B(Entrada_2[7]), .S(Key), .Y(Saida[7]));
endmodule

module Multiplexer_8x1_8bit (
  input  [7:0] Input_1,
  input  [7:0] Input_2,
  input  [7:0] Input_3,
  input  [7:0] Input_4,
  input  [7:0] Input_5,
  input  [7:0] Input_6,
  input  [7:0] Input_7,
  input  [7:0] Input_8,
  input  [2:0] Key,
  output [7:0] \Saída 
);

  wire [7:0] multiplexer_2_in_1_out_8bit_1_saida, multiplexer_2_in_1_out_8bit_2_saida,
       multiplexer_2_in_1_out_8bit_3_saida, multiplexer_2_in_1_out_8bit_4_saida,
       multiplexer_2_in_1_out_8bit_5_saida, multiplexer_2_in_1_out_8bit_6_saida;

  Multiplexer_2_in_1_out__8bit multiplexer_2_in_1_out_8bit_1 (
    .Entrada_1(Input_1), .Entrada_2(Input_2), .Key(Key[0]), .Saida(multiplexer_2_in_1_out_8bit_1_saida));
  Multiplexer_2_in_1_out__8bit multiplexer_2_in_1_out_8bit_2 (
    .Entrada_1(Input_3), .Entrada_2(Input_4), .Key(Key[0]), .Saida(multiplexer_2_in_1_out_8bit_2_saida));
  Multiplexer_2_in_1_out__8bit multiplexer_2_in_1_out_8bit_3 (
    .Entrada_1(Input_5), .Entrada_2(Input_6), .Key(Key[0]), .Saida(multiplexer_2_in_1_out_8bit_3_saida));
  Multiplexer_2_in_1_out__8bit multiplexer_2_in_1_out_8bit_4 (
    .Entrada_1(Input_7), .Entrada_2(Input_8), .Key(Key[0]), .Saida(multiplexer_2_in_1_out_8bit_4_saida));
  Multiplexer_2_in_1_out__8bit multiplexer_2_in_1_out_8bit_5 (
    .Entrada_1(multiplexer_2_in_1_out_8bit_1_saida), .Entrada_2(multiplexer_2_in_1_out_8bit_2_saida),
    .Key(Key[1]), .Saida(multiplexer_2_in_1_out_8bit_5_saida));
  Multiplexer_2_in_1_out__8bit multiplexer_2_in_1_out_8bit_6 (
    .Entrada_1(multiplexer_2_in_1_out_8bit_3_saida), .Entrada_2(multiplexer_2_in_1_out_8bit_4_saida),
    .Key(Key[1]), .Saida(multiplexer_2_in_1_out_8bit_6_saida));
  Multiplexer_2_in_1_out__8bit multiplexer_2_in_1_out_8bit_7 (
    .Entrada_1(multiplexer_2_in_1_out_8bit_5_saida), .Entrada_2(multiplexer_2_in_1_out_8bit_6_saida),
    .Key(Key[2]), .Saida(\Saída ));
endmodule

module Deslocador_2bit (
  input  [7:0] in_1,
  input  Shift_Left_or_Right,
  output [7:0] out_3
);

  wire [7:0] deslocador_1bit_1_saida;

  Deslocador_1bit deslocador_1bit_1 (.in_1(in_1), .Clock(Shift_Left_or_Right), .saida(deslocador_1bit_1_saida));
  Deslocador_1bit deslocador_1bit_2 (.in_1(deslocador_1bit_1_saida), .Clock(Shift_Left_or_Right), .saida(out_3));
endmodule
